// Logisim project item_a.circ as structural Verilog: 1 circuit, main circuit item_A
module item_A (
  input  A,
  input  B,
  input  C,
  output S
);

  wire and_1_out, not_1_out;

  not not_1 (not_1_out, A);
  and and_1 (and_1_out, not_1_out, B);
  or or_1 (S, and_1_out, C);
endmodule
