// Logisim project item_c.circ as structural Verilog: 1 circuit, main circuit item_C
module item_C (
  input  A,
  input  B,
  input  C,
  input  D,
  output S
);

  wire or_1_out;

  or or_1 (or_1_out, C, D);
  nand nand_1 (S, A, B, or_1_out);
endmodule
