// Logisim project item_d.circ as structural Verilog: 1 circuit, main circuit item_D
module item_D (
  input  A,
  input  B,
  input  C,
  output x,
  output y
);

  wire and_1_out, and_2_out, and_3_out, or_1_out, xor_1_out;

  and and_1 (and_1_out, A, B);
  and and_2 (and_2_out, B, C);
  xor xor_1 (xor_1_out, A, B);
  or or_1 (or_1_out, and_1_out, and_2_out);
  and and_3 (and_3_out, A, C);
  xor xor_2 (x, xor_1_out, C);
  or or_2 (y, or_1_out, and_3_out);
endmodule
