// Logisim project questao_2_a.circ as structural Verilog: 1 circuit, main circuit bobonica
module bobonica (
  input  a,
  input  b,
  input  c,
  output X
);

  wire nor_1_out, not_1_out, not_2_out;

  not not_1 (not_1_out, a);
  not not_2 (not_2_out, b);
  nor nor_1 (nor_1_out, not_1_out, not_2_out);
  and and_1 (X, nor_1_out, c);
endmodule
