// Logisim project questao_4.circ as structural Verilog: 1 circuit, main circuit main
module main (
  input  H,
  input  T,
  input  U,
  input  F,
  output A
);

  wire and_1_out, and_2_out, and_3_out, and_4_out;

  and and_1 (and_1_out, H, T);
  and and_2 (and_2_out, H, T, U);
  and and_3 (and_3_out, T, F, U);
  and and_4 (and_4_out, U, F);
  or or_1 (A, and_1_out, and_2_out, and_3_out, and_4_out);
endmodule
