// Logisim project questao05.circ as structural Verilog: 1 circuit, main circuit 5
module _5 (
  input  B2,
  input  B1,
  input  B0,
  output Y3,
  output Y2,
  output Y1,
  output Y0
);

  wire and_3_out, and_4_out, and_5_out, and_6_out, not_1_out, not_2_out, not_3_out, not_4_out, or_1_out;

  and and_1 (Y3, B2, B1);
  not not_1 (not_1_out, B1);
  not not_2 (not_2_out, B2);
  not not_3 (not_3_out, B1);
  and and_2 (Y2, B2, not_1_out);
  and and_3 (and_3_out, not_2_out, not_3_out);
  not not_4 (not_4_out, B0);
  and and_4 (and_4_out, and_3_out, not_4_out);
  and and_5 (and_5_out, B1, B0);
  or or_1 (or_1_out, and_4_out, and_5_out);
  and and_6 (and_6_out, B2, B0);
  or or_2 (Y1, or_1_out, and_6_out);

  assign Y0 = 1'b1;

  // Notes on the sheet:
  //   Y3 = B2 B1
  //   Y2 = B2 ~B1
  //   Y0 = 1
  //   Y1 = ~B2 ~B1 ~B0 + B1 B0 + B2 B0
endmodule
